# Fritzing sketch Schema (saved by Fritzing 0.9.3b)
breadboards: 1

parts:
  Part1 = Arduino Pro Mini (5V)
  Part2 = Bluetooth HC-05 Macho
  R1 = Resistor [tolerance=±5% resistance=1k package="0402 [SMD]"]  # not connected
  R2 = Resistor [tolerance=±5% resistance=2.2k package="0402 [SMD]"]  # not connected
  M1 = DC Motor
  M2 = DC Motor
  Use_small_version_of_the_L298N1 = H-Bridge with L298N
  7_4_Volt_LiPo1 = Power Jack [package=power_jack_slot]

nets:
  N1: Part1.RAW, 7_4_Volt_LiPo1.GND
  N2: Part1.GND, 7_4_Volt_LiPo1.GNDBREAK
  VCC: Part1.VCC, Part2.VCC
  N3: M1.pin_1, Use_small_version_of_the_L298N1.M2-02
  N4: M1.pin_2, Use_small_version_of_the_L298N1.M2-01
  N5: M2.pin_1, Use_small_version_of_the_L298N1.M1-02
  N6: M2.pin_2, Use_small_version_of_the_L298N1.M1-01

custom parts:
  H-Bridge with L298N: h-bridge
